// Logisim project Adder1.circ as structural Verilog: 1 circuit, main circuit main
module main (
  input  Carry_In,
  input  X,
  input  Y,
  output Sum,
  output Carry_Out
);

  wire and_1_out, and_2_out, xor_1_out;

  and and_1 (and_1_out, X, Y);
  xor xor_1 (xor_1_out, X, Y);
  or or_1 (Carry_Out, and_1_out, and_2_out);
  and and_2 (and_2_out, Carry_In, xor_1_out);
  xor xor_2 (Sum, Carry_In, xor_1_out);
endmodule
