// Logisim project Adder4.circ as structural Verilog: 1 circuit, main circuit Adder4
module Adder4 (
  input  [3:0] a,
  input  [3:0] b,
  output [3:0] Sum,
  output Carry_Out
);

  wire Adder_1_carry_out, Adder_2_carry_out, Adder_3_carry_out;

  Adder1_main Adder_4 (.Carry_In(Adder_3_carry_out), .X(a[3]), .Y(b[3]), .Sum(Sum[3]), .Carry_Out(Carry_Out));
  Adder1_main Adder_3 (.Carry_In(Adder_2_carry_out), .X(a[2]), .Y(b[2]), .Sum(Sum[2]), .Carry_Out(Adder_3_carry_out));
  Adder1_main Adder_1 (.Carry_In(1'b0), .X(a[0]), .Y(b[0]), .Sum(Sum[0]), .Carry_Out(Adder_1_carry_out));
  Adder1_main Adder_2 (.Carry_In(Adder_1_carry_out), .X(a[1]), .Y(b[1]), .Sum(Sum[1]), .Carry_Out(Adder_2_carry_out));
endmodule
