// Logisim project Alu1.circ as structural Verilog: 1 circuit, main circuit alu1
module alu1 (
  input  a,
  input  b,
  input  carryIn,
  input  [1:0] control,
  output carryOut,
  output result
);

  wire adder1_1_carryout, adder1_1_sum, and_1_out, multiplexer_1_out, not_1_out, or_1_out;

  not not_1 (not_1_out, b);
  Multiplexer #(.select(2), .enable("false")) multiplexer_1 (
    .in0(1'b0), .in1(1'b0), .in2(b), .in3(not_1_out), .out(multiplexer_1_out), .sel(control));
  adder1 adder1_1 (.carryIn(carryIn), .x(a), .y(multiplexer_1_out), .sum(adder1_1_sum), .carryOut(adder1_1_carryout));
  and and_1 (and_1_out, a, b);
  or or_1 (or_1_out, a, b);
  Multiplexer #(.select(2), .enable("false")) multiplexer_2 (
    .in0(and_1_out), .in1(or_1_out), .in2(adder1_1_sum), .in3(adder1_1_sum), .out(result), .sel(control));
  Multiplexer #(.select(2), .enable("false")) multiplexer_3 (
    .in0(1'b0), .in1(1'b0), .in2(adder1_1_carryout), .in3(adder1_1_carryout), .out(carryOut), .sel(control));

  // Notes on the sheet:
  //   AND
  //   OR
  //   Add/Sub
endmodule
