// Logisim project Alu4.circ as structural Verilog: 1 circuit, main circuit main
module main (
  input  [3:0] a,
  input  [3:0] b,
  input  [1:0] control,
  output overflow,
  output zero,
  output carryOut,
  output [3:0] result
);

  wire alu0_carryout, alu1_carryout, alu2_carryout, and_1_out, and_2_out, multiplexer_1_out, not_1_out,
       not_2_out, not_3_out, not_4_out, not_5_out, or_1_out;

  Multiplexer #(.select(2), .enable("false")) multiplexer_1 (
    .in0(1'b0), .in1(1'b0), .in2(1'b0), .in3(1'b1), .out(multiplexer_1_out), .sel(control));
  alu1 alu0 (
    .a(a[0]), .b(b[0]), .carryIn(multiplexer_1_out), .control(control), .carryOut(alu0_carryout),
    .result(result[0]));
  alu1 alu1 (
    .a(a[1]), .b(b[1]), .carryIn(alu0_carryout), .control(control), .carryOut(alu1_carryout),
    .result(result[1]));
  alu1 alu2 (
    .a(a[2]), .b(b[2]), .carryIn(alu1_carryout), .control(control), .carryOut(alu2_carryout),
    .result(result[2]));
  alu1 alu3 (.a(a[3]), .b(b[3]), .carryIn(alu2_carryout), .control(control), .carryOut(carryOut), .result(result[3]));
  or or_1 (or_1_out, alu2_carryout, carryOut);
  and and_1 (and_1_out, alu2_carryout, result[3]);
  not not_1 (not_1_out, and_1_out);
  not not_2 (not_2_out, result[0]);
  not not_3 (not_3_out, result[1]);
  not not_4 (not_4_out, result[2]);
  not not_5 (not_5_out, result[3]);
  and and_2 (and_2_out, or_1_out, not_1_out);
  and and_3 (zero, not_2_out, not_3_out, not_4_out, not_5_out);
  Multiplexer #(.select(2), .enable("false")) multiplexer_2 (
    .in0(1'b0), .in1(1'b0), .in2(and_2_out), .in3(and_2_out), .out(overflow), .sel(control));

  // Notes on the sheet:
  //   Sub 2s Comp
  //   Overflow Check
endmodule
