// Logisim project TLogisim.circ as structural Verilog: 1 circuit, main circuit main
module main (
  input  a,
  input  a_2,
  input  a_3,
  input  b,
  input  b_2,
  input  a_4,
  input  a_5,
  input  b_3,
  input  b_4,
  input  a_6,
  input  a_7,
  input  b_5,
  input  b_6,
  input  a_8,
  input  a_9,
  input  b_7,
  input  b_8,
  input  s,
  input  [3:0] a_10,
  input  c,
  input  d,
  input  [1:0] s_2,
  input  [1:0] s_3,
  input  s_4,
  input  [1:0] s_5,
  input  [1:0] s_6,
  output c_2,
  output c_3,
  output c_4,
  output c_5,
  output c_6,
  output c_7,
  output c_8,
  output c_9,
  output e,
  output e_2,
  output [3:0] c_10,
  output c_11,
  output c_12,
  output d_2,
  output d_3,
  output e_3,
  output f
);

  not not_1 (c_2, a);
  and and_1 (c_3, a_2, b);
  or or_1 (c_5, a_4, b_3);
  xor xor_1 (c_7, a_6, b_5);
  Multiplexer multiplexer_1 (.in0(a_8), .in1(b_7), .out(c_9), .sel(s));  // open: en
  Decoder decoder_1 (.out0(c_12), .out1(d_3), .sel(s_4));  // open: en
  nand nand_1 (c_4, a_3, b_2);
  nor nor_1 (c_6, a_5, b_4);
  xnor xnor_1 (c_8, a_7, b_6);
  Multiplexer #(.select(2)) multiplexer_2 (.in0(a_9), .in1(b_8), .in2(c), .in3(d), .out(e), .sel(s_2));  // open: en
  Decoder #(.select(2)) decoder_2 (.out0(c_11), .out1(d_2), .out2(e_3), .out3(f), .sel(s_5));  // open: en
  Decoder #(.select(2)) decoder_3 (
    .out0(c_10[0]), .out1(c_10[1]), .out2(c_10[2]), .out3(c_10[3]), .sel(s_6));  // open: en
  Multiplexer #(.select(2)) multiplexer_3 (
    .in0(a_10[0]), .in1(a_10[1]), .in2(a_10[2]), .in3(a_10[3]), .out(e_2), .sel(s_3));  // open: en

  // Notes on the sheet:
  //   # Test Logisim Simulator
  //   # Progrm-ID: TLogicsim.circ
  //   # Author: Kuo-pao Yang
  //   # Simulator: Logisim 2.7.1
  //   # Test NOT, And/Nand, Or/Nor, Xor/Xnor, Mux, and Decoder
  //   # Test NOT:  c = NOT a 
  //   # Test And2: c = a AND b
  //   # Test OR2: c = a OR b
  //   # Test XOR2: c = a XOR b
  //   # Test Mux2: if (s = 0) c = a; else c = b 
  //   # Test Decd2: 1 hot; if (s = 0) c = 1; else d = 1
  //   # Test Nand2: c = a NAND b
  //   # Test NOR2: c = a NOR b
  //   # Test XNOR2: c = a XNOR b
  //   # Test Mux4: if (s = 00) e = a; (s = 01) e = b; (s = 10) e = c; (s = 11) e = d 
  //   # Test Decd4: 1 hot; if (s = 00) c = 1; (s = 01) d = 1; (s = 10) e = 1; (s = 11) f = 1 
  //   # Test Splitter Mux4
  //   # Test Splitter Decd4
endmodule
